// Logisim project 2.circ as structural Verilog: 1 circuit, main circuit main
module main (
  input  in_1,
  input  in_2,
  output out_3,
  output out_4,
  output out_5
);

  wire and_1_out, and_2_out, not_1_out, or_1_out, t_ff_1_qn, t_ff_2_qn;

  not not_1 (not_1_out, in_1);
  and and_1 (and_1_out, in_1, in_1);
  and and_2 (and_2_out, t_ff_2_qn, t_ff_1_qn);
  or or_1 (or_1_out, and_2_out, and_1_out);
  T_Flip_Flop t_ff_1 (.clk(in_2), .T(or_1_out), .Q(in_1), .Qn(t_ff_1_qn));  // open: preset, reset, en
  T_Flip_Flop t_ff_2 (.clk(in_2), .T(in_1), .Q(out_4), .Qn(t_ff_2_qn));  // open: preset, reset, en
  and and_3 (out_3, in_1, t_ff_2_qn);

  assign out_5 = in_1;
endmodule
