// Logisim project LAB 7A Syed Mozahidul Islam.circ as structural Verilog: 5 circuits, main circuit main
module main (
);


  // Notes on the sheet:
  //   Syed Mozahidul Islam
  //   2111672642
endmodule

module JK_Flipflop_implemented_using_AND_and_NOR_gates (
  input  k,
  input  J,
  output Q,
  output Q_prime
);

  wire and_1_out, and_2_out, clock_1_out;

  Clock clock_1 (.out(clock_1_out));
  and and_1 (and_1_out, clock_1_out, J, Q_prime);
  and and_2 (and_2_out, Q, k, clock_1_out);
  nor nor_1 (Q, and_2_out, Q_prime);
  nor nor_2 (Q_prime, Q, and_1_out);

  // Notes on the sheet:
  //   Clock Pulse
  //                                                      JK Flipflop implemented using AND and NOR gates
  //   Syed Mozahidul slam
  //   2111672642
endmodule

module T_flipflop_constructed_using_JK_flipflop (
  input  in_1,
  input  in_2,
  input  in_3,
  input  in_4,
  output Q,
  output Q_prime
);

  wire clock_1_out, t_ff_1_qn;

  T_Flip_Flop t_ff_1 (.Qn(t_ff_1_qn));  // open: clk, T, Q, preset, reset, en
  Clock clock_1 (.out(clock_1_out));
  J_K_Flip_Flop j_k_ff_1 (
    .J(in_1), .clk(clock_1_out), .K(in_2), .Q(Q), .Qn(Q_prime), .en(in_3), .reset(in_4));  // open: preset

  // Notes on the sheet:
  //   K
  //   T flipflop constructed using Jk flipflop
  //   Syed Mozahidul Islam
  //   2111672642
endmodule

module D_flipflop_constructed_using_JK_flipflop (
  input  in_1,
  input  in_2,
  input  in_3,
  input  in_4,
  output out_5,
  output out_6
);

  wire clock_1_out, not_1_out;

  Clock clock_1 (.out(clock_1_out));
  not not_1 (not_1_out, in_1);
  J_K_Flip_Flop j_k_ff_1 (
    .J(in_1), .clk(clock_1_out), .K(in_2), .Q(out_5), .Qn(out_6), .en(in_3), .reset(in_4));  // open: preset

  // Notes on the sheet:
  //   D flipflop constructed using JK flipflop
  //   Syed Mozahidul Islam
  //   2111672642
endmodule

module Right_shift_register (
  input  in_1
);

  wire clock_1_out, d_ff_1_q, d_ff_2_q, d_ff_3_q, d_ff_4_q;

  Clock clock_1 (.out(clock_1_out));
  LED led_1 (.in(d_ff_1_q));
  D_Flip_Flop d_ff_1 (.clk(clock_1_out), .D(in_1), .Q(d_ff_1_q));  // open: Qn, preset, en, reset
  LED led_2 (.in(d_ff_2_q));
  LED led_3 (.in(d_ff_3_q));
  D_Flip_Flop d_ff_2 (.clk(clock_1_out), .D(d_ff_1_q), .Q(d_ff_2_q));  // open: Qn, preset, en, reset
  D_Flip_Flop d_ff_3 (.clk(clock_1_out), .D(d_ff_2_q), .Q(d_ff_3_q));  // open: Qn, preset, en, reset
  LED led_4 (.in(d_ff_4_q));
  D_Flip_Flop d_ff_4 (.clk(clock_1_out), .D(d_ff_3_q), .Q(d_ff_4_q));  // open: Qn, preset, en, reset

  // Notes on the sheet:
  //                                               Clock Pulse
  //                                                                                                Right Shift Register
  //   Syed Mozahidul Islam
  //   2111672642
endmodule
