// Logisim project LAB 7B Syed Mozahidul Islam.circ as structural Verilog: 3 circuits, main circuit main
module main (
  input  in_1,
  input  in_2,
  input  in_3,
  input  in_4
);

  wire bcd_decoder_1_a_2, bcd_decoder_1_b_2, bcd_decoder_1_c_2, bcd_decoder_1_d_2, bcd_decoder_1_e,
       bcd_decoder_1_f, bcd_decoder_1_g;

  BCD_Decoder bcd_decoder_1 (
    .A(in_1), .B(in_2), .C(in_3), .D(in_4), .a_2(bcd_decoder_1_a_2), .b_2(bcd_decoder_1_b_2),
    .c_2(bcd_decoder_1_c_2), .d_2(bcd_decoder_1_d_2), .e(bcd_decoder_1_e), .f(bcd_decoder_1_f),
    .g(bcd_decoder_1_g));
  _7_Segment_Display u_7_segment_display_1 (
    .g(bcd_decoder_1_g), .f(bcd_decoder_1_f), .a(bcd_decoder_1_a_2), .b(bcd_decoder_1_b_2),
    .e(bcd_decoder_1_e), .d(bcd_decoder_1_d_2), .c(bcd_decoder_1_c_2));  // open: dp

  // Notes on the sheet:
  //   Syed Mozahidul Islam
  //   2111642672
endmodule

module BCD_Decoder (
  input  A,
  input  B,
  input  C,
  input  D,
  output a_2,
  output b_2,
  output c_2,
  output d_2,
  output e,
  output f,
  output g
);

  wire and_1_out, and_2_out, and_3_out, and_4_out, and_5_out, and_6_out, and_7_out, and_8_out, and_9_out,
       and_10_out, and_11_out, and_12_out, and_13_out, and_14_out, and_15_out, and_16_out, not_1_out,
       not_2_out, not_3_out, not_4_out, not_5_out, not_6_out, not_7_out, not_8_out, not_9_out, not_10_out,
       not_11_out, not_12_out, not_13_out, not_14_out, not_15_out, not_16_out, not_17_out, not_18_out,
       not_19_out, not_20_out, not_21_out;

  not not_1 (not_1_out, B);
  and and_1 (and_1_out, not_1_out, not_2_out);
  not not_2 (not_2_out, D);
  and and_2 (and_2_out, B, D);
  not not_3 (not_3_out, B);
  not not_4 (not_4_out, C);
  not not_5 (not_5_out, D);
  not not_6 (not_6_out, C);
  not not_7 (not_7_out, B);
  and and_3 (and_3_out, not_7_out, not_8_out);
  not not_8 (not_8_out, D);
  not not_9 (not_9_out, B);
  and and_4 (and_4_out, C, not_10_out);
  not not_10 (not_10_out, D);
  not not_11 (not_11_out, C);
  not not_12 (not_12_out, B);
  and and_5 (and_5_out, not_12_out, not_13_out);
  not not_13 (not_13_out, D);
  not not_14 (not_14_out, D);
  not not_15 (not_15_out, C);
  and and_6 (and_6_out, not_15_out, not_16_out);
  not not_16 (not_16_out, D);
  and and_7 (and_7_out, B, not_17_out);
  not not_17 (not_17_out, C);
  not not_18 (not_18_out, D);
  not not_19 (not_19_out, B);
  and and_8 (and_8_out, not_19_out, C);
  and and_9 (and_9_out, B, not_20_out);
  not not_20 (not_20_out, C);
  not not_21 (not_21_out, D);
  and and_10 (and_10_out, not_9_out, C);
  and and_11 (and_11_out, B, not_11_out, D);
  and and_12 (and_12_out, not_4_out, not_5_out);
  and and_13 (and_13_out, C, D);
  and and_14 (and_14_out, B, not_18_out);
  and and_15 (and_15_out, B, not_21_out);
  and and_16 (and_16_out, C, not_14_out);
  or or_1 (a_2, and_1_out, C, and_2_out, A);
  or or_2 (b_2, not_3_out, and_12_out, and_13_out);
  or or_3 (c_2, not_6_out, D, B);
  or or_4 (d_2, and_3_out, and_10_out, and_4_out, and_11_out, A);
  or or_5 (e, and_5_out, and_16_out);
  or or_6 (f, and_6_out, and_7_out, and_14_out, A);
  or or_7 (g, and_8_out, and_9_out, and_15_out, A);

  // Notes on the sheet:
  //   Syed Mozahidul Islam
  //   2111642672
endmodule

module Test (
  input  D,
  input  C,
  input  B,
  input  A,
  output a_2,
  output b_2,
  output c_2,
  output d_2,
  output e,
  output f,
  output g
);

  wire and_1_out, and_2_out, and_3_out, and_4_out, and_5_out, and_6_out, and_7_out, and_8_out, and_9_out,
       and_10_out, and_11_out, and_12_out, and_13_out, and_14_out, and_15_out, and_16_out, and_17_out,
       and_18_out, and_19_out, and_20_out, and_21_out, and_22_out, and_23_out, and_24_out, and_25_out,
       and_26_out, and_27_out, and_28_out, and_29_out, and_30_out, and_31_out, and_32_out, not_1_out,
       not_2_out, not_3_out, not_4_out, or_1_out, or_2_out, or_3_out, or_4_out, or_5_out, or_6_out, or_7_out,
       or_8_out, xor_1_out;

  not not_1 (not_1_out, D);
  not not_2 (not_2_out, C);
  not not_3 (not_3_out, B);
  not not_4 (not_4_out, A);
  and and_1 (and_1_out, D, not_2_out, not_3_out);
  and and_2 (and_2_out, not_1_out, C, A);
  and and_3 (and_3_out, D, not_4_out);
  and and_4 (and_4_out, not_1_out, B);
  and and_5 (and_5_out, C, B);
  and and_6 (and_6_out, not_2_out, not_4_out);
  and and_7 (and_7_out, not_1_out, not_3_out, not_4_out);
  and and_8 (and_8_out, not_1_out, B, A);
  and and_9 (and_9_out, D, not_3_out, A);
  and and_10 (and_10_out, not_2_out, not_3_out);
  and and_11 (and_11_out, not_1_out, not_3_out);
  and and_12 (and_12_out, not_1_out, A);
  and and_13 (and_13_out, not_3_out, A);
  xor xor_1 (xor_1_out, D, C);
  and and_14 (and_14_out, not_1_out, not_2_out, not_4_out);
  and and_15 (and_15_out, not_2_out, B, A);
  and and_16 (and_16_out, C, not_3_out, A);
  and and_17 (and_17_out, C, B, not_4_out);
  and and_18 (and_18_out, D, not_3_out);
  and and_19 (and_19_out, not_2_out, not_4_out);
  and and_20 (and_20_out, B, not_4_out);
  and and_21 (and_21_out, D, B);
  and and_22 (and_22_out, D, C);
  and and_23 (and_23_out, not_1_out, C, not_3_out);
  and and_24 (and_24_out, not_3_out, not_4_out);
  and and_25 (and_25_out, C, not_4_out);
  and and_26 (and_26_out, D, not_2_out);
  and and_27 (and_27_out, D, B);
  and and_28 (and_28_out, not_1_out, C, not_3_out);
  and and_29 (and_29_out, not_2_out, B);
  and and_30 (and_30_out, B, not_4_out);
  and and_31 (and_31_out, D, not_2_out);
  and and_32 (and_32_out, D, A);
  or or_1 (or_1_out, and_6_out, and_7_out, and_8_out);
  or or_2 (or_2_out, and_11_out, and_12_out, and_13_out);
  or or_3 (or_3_out, and_14_out, and_15_out, and_16_out);
  or or_4 (or_4_out, and_19_out, and_20_out, and_21_out);
  or or_5 (or_5_out, and_1_out, and_2_out, and_3_out);
  or or_6 (or_6_out, and_4_out, and_5_out, and_6_out);
  or or_7 (or_7_out, and_23_out, and_24_out, and_25_out);
  or or_8 (or_8_out, and_28_out, and_29_out, and_30_out);
  or or_9 (b_2, or_1_out, and_9_out, and_10_out);
  or or_10 (c_2, or_2_out, xor_1_out);
  or or_11 (a_2, or_5_out, or_6_out);
  or or_12 (d_2, or_3_out, and_17_out, and_18_out);
  or or_13 (e, or_4_out, and_22_out);
  or or_14 (f, or_7_out, and_26_out, and_27_out);
  or or_15 (g, or_8_out, and_31_out, and_32_out);
  _7_Segment_Display u_7_segment_display_1 (.g(g), .f(f), .a(a_2), .b(b_2), .e(e), .d(d_2), .c(c_2));  // open: dp
endmodule
