// Logisim project LAB 8 Syed Mozahidul Islam.circ as structural Verilog: 3 circuits, main circuit Sequential Circuit JK-FlipFlop
module Sequential_Circuit_JK_FlipFlop (
  input  in_1,
  input  in_2,
  input  in_3,
  output out_4,
  output out_5,
  output out_6,
  output out_7,
  output out_8
);

  wire and_1_out, clock_1_out, not_1_out;

  not not_1 (not_1_out, in_1);
  Clock clock_1 (.out(clock_1_out));
  and and_1 (and_1_out, out_4, not_1_out);
  J_K_Flip_Flop A (
    .J(in_1), .clk(clock_1_out), .K(in_1), .Q(out_4), .Qn(out_5), .preset(in_3), .en(in_3), .reset(in_2));
  J_K_Flip_Flop B (
    .J(and_1_out), .clk(clock_1_out), .K(in_1), .Q(out_6), .Qn(out_7), .preset(in_3), .en(in_3), .reset(in_2));
  and and_2 (out_8, out_5, in_1);

  // Notes on the sheet:
  //   Syed Mozahidul Islam
  //   2111672642
endmodule

module Sequential_CircuitT_T_FlipFlop (
  input  in_1,
  input  in_2,
  input  in_3,
  output out_4,
  output out_5,
  output out_6,
  output out_7,
  output out_8
);

  wire and_1_out, and_2_out, clock_1_out, not_1_out, or_1_out;

  not not_1 (not_1_out, in_1);
  Clock clock_1 (.out(clock_1_out));
  and and_1 (and_1_out, out_4, out_6);
  or or_1 (or_1_out, and_1_out, and_2_out);
  and and_2 (and_2_out, out_5, not_1_out, out_7);
  T_Flip_Flop t_ff_1 (.clk(clock_1_out), .T(out_6), .Q(out_4), .Qn(out_5), .preset(in_3), .reset(in_2), .en(in_3));
  T_Flip_Flop t_ff_2 (.clk(clock_1_out), .T(or_1_out), .Q(out_6), .Qn(out_7), .preset(in_3), .reset(in_2), .en(in_3));
  and and_3 (out_8, out_6, not_1_out);

  // Notes on the sheet:
  //   Syed Mozahidul Islam
  //   2111672642
endmodule

module Sequential_Circuit_D_FlipFlop (
  input  in_1,
  input  in_2,
  input  in_3,
  output A,
  output A_prime,
  output B,
  output B_prime,
  output Y
);

  wire and_1_out, clock_1_out, not_1_out, xor_1_out;

  not not_1 (not_1_out, in_1);
  xor xor_1 (xor_1_out, in_1, B);
  Clock clock_1 (.out(clock_1_out));
  D_Flip_Flop u_A (.clk(clock_1_out), .D(xor_1_out), .Q(A), .Qn(A_prime), .preset(in_3), .en(in_3), .reset(in_2));
  D_Flip_Flop u_B (.clk(clock_1_out), .D(and_1_out), .Q(B), .Qn(B_prime), .preset(in_3), .en(in_3), .reset(in_2));
  and and_1 (and_1_out, not_1_out, B_prime);
  and and_2 (Y, B, not_1_out);

  // Notes on the sheet:
  //   Syed Mozahidul Islam
  //   2111672642
endmodule
