// Logisim project Lab 1 Digital Logic Gates.circ as structural Verilog
module JK_Flip_Flop (
  input  X,
  input  Clock,
  output Y,
  output A,
  output B
);

  wire and_1_out, j_k_ff_1_qn, not_1_out;

  not not_1 (not_1_out, X);
  J_K_Flip_Flop j_k_ff_1 (.J(X), .clk(Clock), .K(X), .Q(A), .Qn(j_k_ff_1_qn));  // open: preset, en, reset
  buf and_1 (and_1_out, X);  // AND_Gate
  buf and_2 (Y, j_k_ff_1_qn);  // AND_Gate
  J_K_Flip_Flop j_k_ff_2 (.J(and_1_out), .clk(Clock), .K(X), .Q(B));  // open: Qn, preset, en, reset
endmodule

module T_Flip_Flop (
  input  in_1,
  input  in_2,
  output out_3,
  output out_4,
  output out_5
);

  wire and_1_out, and_2_out, not_1_out, or_1_out, t_ff_1_qn, t_ff_2_qn;

  not not_1 (not_1_out, in_1);
  and and_1 (and_1_out, in_1, in_1);
  and and_2 (and_2_out, t_ff_2_qn, t_ff_1_qn);
  or or_1 (or_1_out, and_2_out, and_1_out);
  T_Flip_Flop_part t_ff_1 (.clk(in_2), .T(or_1_out), .Q(in_1), .Qn(t_ff_1_qn));  // open: preset, reset, en
  T_Flip_Flop_part t_ff_2 (.clk(in_2), .T(in_1), .Q(out_4), .Qn(t_ff_2_qn));  // open: preset, reset, en
  and and_3 (out_3, in_1, t_ff_2_qn);

  assign out_5 = in_1;
endmodule

module D_Flip_Flop (
  input  in_1,
  input  Clock,
  output out_3,
  output out_4,
  output out_5
);

  wire and_1_out, and_3_out, d_ff_1_qn, not_1_out, or_1_out;

  not not_1 (not_1_out, in_1);
  and and_1 (and_1_out, out_3, not_1_out);
  and and_2 (out_4, in_1, d_ff_1_qn);
  and and_3 (and_3_out, d_ff_1_qn, not_1_out);
  or or_1 (or_1_out, and_1_out, out_4);
  D_Flip_Flop_part d_ff_1 (.clk(Clock), .D(or_1_out), .Q(out_3), .Qn(d_ff_1_qn));  // open: preset, en, reset
  D_Flip_Flop_part d_ff_2 (.clk(Clock), .D(and_3_out), .Q(out_5));  // open: Qn, preset, en, reset
endmodule
