// Logisim project Lab 6.circ as structural Verilog: 1 circuit, main circuit main
module main (
  input  X,
  input  Y,
  input  Cin,
  output out_4,
  output out_5
);

  wire and_1_out, and_2_out, and_3_out, and_4_out, and_5_out, and_6_out, not_1_out, not_2_out, not_3_out,
       not_4_out, or_1_out;

  not not_1 (not_1_out, X);
  not not_2 (not_2_out, Y);
  and and_1 (and_1_out, X, not_2_out);
  and and_2 (and_2_out, X, Y);
  and and_3 (and_3_out, not_1_out, not_1_out, not_1_out, Y, Y);
  or or_1 (or_1_out, and_3_out, and_3_out, and_1_out, and_1_out);
  not not_3 (not_3_out, Cin);
  not not_4 (not_4_out, or_1_out);
  and and_4 (and_4_out, or_1_out, Cin);
  and and_5 (and_5_out, not_4_out, not_4_out, Cin);
  and and_6 (and_6_out, or_1_out, not_3_out);
  or or_2 (out_5, and_4_out, and_2_out);
  or or_3 (out_4, and_5_out, and_5_out, and_6_out, and_6_out);

  // Notes on the sheet:
  //   Shaikh Farhana Supti
  //   2112266642
endmodule
