// Logisim project Lab3 Universal Gate.circ as structural Verilog: 1 circuit, main circuit main
module main (
  input  in_1,
  input  Clock,
  output out_3,
  output out_4,
  output out_5
);

  wire and_1_out, and_3_out, d_ff_1_qn, not_1_out, or_1_out;

  not not_1 (not_1_out, in_1);
  and and_1 (and_1_out, out_3, not_1_out);
  and and_2 (out_4, in_1, d_ff_1_qn);
  and and_3 (and_3_out, d_ff_1_qn, not_1_out);
  or or_1 (or_1_out, and_1_out, out_4);
  D_Flip_Flop d_ff_1 (.clk(Clock), .D(or_1_out), .Q(out_3), .Qn(d_ff_1_qn));  // open: preset, en, reset
  D_Flip_Flop d_ff_2 (.clk(Clock), .D(and_3_out), .Q(out_5));  // open: Qn, preset, en, reset
endmodule
