// Logisim project Syed Mozahidul Islam LAB2.circ as structural Verilog: 1 circuit, main circuit main
module main (
  input  in_1,
  input  in_2,
  input  in_3
);

  wire nand_1_out, nand_2_out, nand_3_out, nand_4_out;

  nand nand_1 (nand_1_out, in_3, in_3);
  nand nand_2 (nand_2_out, in_1, in_3);
  nand nand_3 (nand_3_out, in_2, nand_1_out);
  nand nand_4 (nand_4_out, nand_2_out, nand_3_out);
  LED led_1 (.in(nand_2_out));
  LED led_2 (.in(nand_4_out));
  LED led_3 (.in(nand_3_out));

  // Notes on the sheet:
  //   PART 2
  //   Syed Mozahidul Islam
  //   2111672642 
  //   Workstation 4
  //   Section 9
endmodule
